// Logisim project flip-flo-d.circ as structural Verilog: 2 circuits, main circuit main
module main (
  input  D,
  output Q,
  output nQ
);

  wire and_1_out, and_2_out, CLOCK_out, not_1_out;

  not not_1 (not_1_out, D);
  Clock CLOCK (.out(CLOCK_out));
  and and_1 (and_1_out, CLOCK_out, not_1_out);
  and and_2 (and_2_out, D, CLOCK_out);
  nor nor_1 (Q, and_1_out, nQ);
  nor nor_2 (nQ, Q, and_2_out);
endmodule

module flip_flod_D_clear_preset (
  input  DATA,
  input  ENABLE,
  output out_3,
  output out_4
);

  wire nand_1_out, nand_2_out, nand_3_out;

  not nand_1 (nand_1_out, DATA);  // NAND_Gate
  nand nand_2 (nand_2_out, DATA, ENABLE);
  nand nand_3 (nand_3_out, ENABLE, nand_1_out);
  nand nand_4 (out_3, nand_2_out, out_4);
  nand nand_5 (out_4, out_3, nand_3_out);
endmodule
