// Logisim project flip-flop-JK.circ as structural Verilog: 1 circuit, main circuit main
module main (
  input  PRESET,
  input  J,
  input  K,
  input  CLEAR,
  output Q,
  output nQ
);

  wire clock_1_out, nand_1_out, nand_2_out, nand_3_out, nand_4_out, nand_5_out, nand_6_out, not_1_out,
       not_2_out, not_3_out;

  Clock clock_1 (.out(clock_1_out));
  nand nand_1 (nand_1_out, nQ, J, clock_1_out);
  not not_1 (not_1_out, clock_1_out);
  nand nand_2 (nand_2_out, clock_1_out, K, Q);
  not not_2 (not_2_out, PRESET);
  not not_3 (not_3_out, CLEAR);
  nand nand_3 (nand_3_out, not_2_out, nand_1_out, nand_4_out);
  nand nand_4 (nand_4_out, nand_3_out, nand_2_out, not_3_out);
  nand nand_5 (nand_5_out, not_3_out, nand_3_out, not_1_out);
  nand nand_6 (nand_6_out, not_1_out, nand_4_out, not_2_out);
  nand nand_7 (Q, not_2_out, nand_5_out, nQ);
  nand nand_8 (nQ, Q, nand_6_out, not_3_out);
endmodule
