// Logisim project banco-registradores.circ as structural Verilog: 9 circuits, main circuit Banco de Registradores
module Banco_de_Registradores (
  input  RESET,
  input  LOAD,
  input  [7:0] ENTRADA,
  input  [2:0] CHAVE,
  input  LOAD_2,
  input  LOAD_3,
  input  CLOCK,
  input  SET,
  input  [2:0] CHAVE_2,
  input  [2:0] CHAVE_3,
  output [7:0] \SAÍDA ,
  output [7:0] \SAÍDA_2 
);

  wire demultiplexador_1_out_4, demultiplexador_1_out_5, demultiplexador_1_out_6, demultiplexador_1_out_7,
       demultiplexador_1_out_8, demultiplexador_1_out_9, demultiplexador_1_out_10, demultiplexador_1_out_11;
  wire [7:0] registrador_8_bits_1_out_5, registrador_8_bits_2_out_5, registrador_8_bits_3_out_5,
       registrador_8_bits_4_out_5, registrador_8_bits_5_out_5, registrador_8_bits_6_out_5,
       registrador_8_bits_7_out_5, registrador_8_bits_8_out_5;

  demultiplexador demultiplexador_1 (
    .LOAD(LOAD_3), .CLOCK(CLOCK), .CHAVE(CHAVE_2), .out_4(demultiplexador_1_out_4),
    .out_5(demultiplexador_1_out_5), .out_6(demultiplexador_1_out_6), .out_7(demultiplexador_1_out_7),
    .out_8(demultiplexador_1_out_8), .out_9(demultiplexador_1_out_9), .out_10(demultiplexador_1_out_10),
    .out_11(demultiplexador_1_out_11));
  Registrador_8_bits registrador_8_bits_1 (
    .out_5(registrador_8_bits_1_out_5), .SET(SET), .CLOCK(demultiplexador_1_out_4), .RESET(RESET),
    .ENTRADA(ENTRADA));
  Registrador_8_bits registrador_8_bits_2 (
    .out_5(registrador_8_bits_2_out_5), .SET(SET), .CLOCK(demultiplexador_1_out_5), .RESET(RESET),
    .ENTRADA(ENTRADA));
  Registrador_8_bits registrador_8_bits_3 (
    .out_5(registrador_8_bits_3_out_5), .SET(SET), .CLOCK(demultiplexador_1_out_6), .RESET(RESET),
    .ENTRADA(ENTRADA));
  Registrador_8_bits registrador_8_bits_4 (
    .out_5(registrador_8_bits_4_out_5), .SET(SET), .CLOCK(demultiplexador_1_out_7), .RESET(RESET),
    .ENTRADA(ENTRADA));
  Registrador_8_bits registrador_8_bits_5 (
    .out_5(registrador_8_bits_5_out_5), .SET(SET), .CLOCK(demultiplexador_1_out_8), .RESET(RESET),
    .ENTRADA(ENTRADA));
  Registrador_8_bits registrador_8_bits_6 (
    .out_5(registrador_8_bits_6_out_5), .SET(SET), .CLOCK(demultiplexador_1_out_9), .RESET(RESET),
    .ENTRADA(ENTRADA));
  Registrador_8_bits registrador_8_bits_7 (
    .out_5(registrador_8_bits_7_out_5), .SET(SET), .CLOCK(demultiplexador_1_out_10), .RESET(RESET),
    .ENTRADA(ENTRADA));
  Registrador_8_bits registrador_8_bits_8 (
    .out_5(registrador_8_bits_8_out_5), .SET(SET), .CLOCK(demultiplexador_1_out_11), .RESET(RESET),
    .ENTRADA(ENTRADA));
  Mult_8x1_8bits mult_8x1_8bits_1 (
    .in_2(registrador_8_bits_1_out_5), .in_3(registrador_8_bits_2_out_5), .in_4(registrador_8_bits_3_out_5),
    .in_5(registrador_8_bits_4_out_5), .in_6(registrador_8_bits_5_out_5), .in_7(registrador_8_bits_6_out_5),
    .in_8(registrador_8_bits_7_out_5), .in_9(registrador_8_bits_8_out_5), .CHAVE(CHAVE), .\SAÍDA (\SAÍDA ),
    .LOAD(LOAD));
  Mult_8x1_8bits mult_8x1_8bits_2 (
    .in_2(registrador_8_bits_1_out_5), .in_3(registrador_8_bits_2_out_5), .in_4(registrador_8_bits_3_out_5),
    .in_5(registrador_8_bits_4_out_5), .in_6(registrador_8_bits_5_out_5), .in_7(registrador_8_bits_6_out_5),
    .in_8(registrador_8_bits_7_out_5), .in_9(registrador_8_bits_8_out_5), .CHAVE(CHAVE_3),
    .\SAÍDA (\SAÍDA_2 ), .LOAD(LOAD_2));
endmodule

module Mult_2x1 (
  input  in_1,
  input  in_2,
  input  load,
  input  in_4,
  output out_5
);

  wire and_1_out, and_2_out, or_1_out;

  and and_1 (and_1_out, in_1, ~in_4);  // AND_Gate
  and and_2 (and_2_out, in_2, in_4);
  or or_1 (or_1_out, and_1_out, and_2_out);
  and and_3 (out_5, or_1_out, load);
endmodule

module Mult_2x1_8_bits (
  input  [7:0] A,
  input  LOAD,
  input  CHAVE,
  input  [7:0] B,
  output [7:0] \SAÍDA 
);

  Mult_2x1 mult_2x1_1 (.in_1(A[0]), .in_2(B[0]), .load(LOAD), .out_5(\SAÍDA [0]), .in_4(CHAVE));
  Mult_2x1 mult_2x1_2 (.in_1(A[1]), .in_2(B[1]), .load(LOAD), .out_5(\SAÍDA [1]), .in_4(CHAVE));
  Mult_2x1 mult_2x1_3 (.in_1(A[2]), .in_2(B[2]), .load(LOAD), .out_5(\SAÍDA [2]), .in_4(CHAVE));
  Mult_2x1 mult_2x1_4 (.in_1(A[3]), .in_2(B[3]), .load(LOAD), .out_5(\SAÍDA [3]), .in_4(CHAVE));
  Mult_2x1 mult_2x1_5 (.in_1(A[4]), .in_2(B[4]), .load(LOAD), .out_5(\SAÍDA [4]), .in_4(CHAVE));
  Mult_2x1 mult_2x1_6 (.in_1(A[5]), .in_2(B[5]), .load(LOAD), .out_5(\SAÍDA [5]), .in_4(CHAVE));
  Mult_2x1 mult_2x1_7 (.in_1(A[6]), .in_2(B[6]), .load(LOAD), .out_5(\SAÍDA [6]), .in_4(CHAVE));
  Mult_2x1 mult_2x1_8 (.in_1(A[7]), .in_2(B[7]), .load(LOAD), .out_5(\SAÍDA [7]), .in_4(CHAVE));
endmodule

module Multi_4x1 (
  input  A,
  input  B,
  input  C,
  input  LOAD,
  input  D,
  input  S1,
  input  S2,
  output \SAÍDA 
);

  wire and_1_out, and_2_out, and_3_out, and_4_out, or_1_out;

  and and_1 (and_1_out, A, ~S1, ~S2);  // AND_Gate
  and and_2 (and_2_out, B, ~S1, S2);  // AND_Gate
  and and_3 (and_3_out, C, S1, ~S2);  // AND_Gate
  and and_4 (and_4_out, D, S1, S2);
  or or_1 (or_1_out, and_1_out, and_2_out, and_3_out, and_4_out);
  and and_5 (\SAÍDA , or_1_out, LOAD);
endmodule

module Multi_4x1_8bits (
  input  LOAD,
  input  [7:0] ENTRADA_A,
  input  [7:0] ENTRADA_B,
  input  [1:0] in_4,
  input  [7:0] ENTRADA_C,
  input  [7:0] ENTRADA_D,
  output [7:0] out_7
);

  Multi_4x1 multi_4x1_1 (
    .A(ENTRADA_A[0]), .B(ENTRADA_B[0]), .C(ENTRADA_C[0]), .LOAD(LOAD), .D(ENTRADA_D[0]), .\SAÍDA (out_7[0]),
    .S1(in_4[0]), .S2(in_4[1]));
  Multi_4x1 multi_4x1_2 (
    .A(ENTRADA_A[1]), .B(ENTRADA_B[1]), .C(ENTRADA_C[1]), .LOAD(LOAD), .D(ENTRADA_D[1]), .\SAÍDA (out_7[1]),
    .S1(in_4[0]), .S2(in_4[1]));
  Multi_4x1 multi_4x1_3 (
    .A(ENTRADA_A[2]), .B(ENTRADA_B[2]), .C(ENTRADA_C[2]), .LOAD(LOAD), .D(ENTRADA_D[2]), .\SAÍDA (out_7[2]),
    .S1(in_4[0]), .S2(in_4[1]));
  Multi_4x1 multi_4x1_4 (
    .A(ENTRADA_A[3]), .B(ENTRADA_B[3]), .C(ENTRADA_C[3]), .LOAD(LOAD), .D(ENTRADA_D[3]), .\SAÍDA (out_7[3]),
    .S1(in_4[0]), .S2(in_4[1]));
  Multi_4x1 multi_4x1_5 (
    .A(ENTRADA_A[5]), .B(ENTRADA_B[5]), .C(ENTRADA_C[5]), .LOAD(LOAD), .D(ENTRADA_D[5]), .\SAÍDA (out_7[5]),
    .S1(in_4[0]), .S2(in_4[1]));
  Multi_4x1 multi_4x1_6 (
    .A(ENTRADA_A[6]), .B(ENTRADA_B[6]), .C(ENTRADA_C[6]), .LOAD(LOAD), .D(ENTRADA_D[6]), .\SAÍDA (out_7[6]),
    .S1(in_4[0]), .S2(in_4[1]));
  Multi_4x1 multi_4x1_7 (
    .A(ENTRADA_A[7]), .B(ENTRADA_B[7]), .C(ENTRADA_C[7]), .LOAD(LOAD), .D(ENTRADA_D[7]), .\SAÍDA (out_7[7]),
    .S1(in_4[0]), .S2(in_4[1]));
  Multi_4x1 multi_4x1_8 (
    .A(ENTRADA_A[4]), .B(ENTRADA_B[4]), .C(ENTRADA_C[4]), .LOAD(LOAD), .D(ENTRADA_D[4]), .\SAÍDA (out_7[4]),
    .S1(in_4[0]), .S2(in_4[1]));
endmodule

module Mult_8x1_8bits (
  input  LOAD,
  input  [7:0] in_2,
  input  [7:0] in_3,
  input  [7:0] in_4,
  input  [7:0] in_5,
  input  [7:0] in_6,
  input  [7:0] in_7,
  input  [7:0] in_8,
  input  [7:0] in_9,
  input  [2:0] CHAVE,
  output [7:0] \SAÍDA 
);

  wire [7:0] multi_4x1_8bits_1_out_7, multi_4x1_8bits_2_out_7;

  Multi_4x1_8bits multi_4x1_8bits_1 (
    .ENTRADA_A(in_2), .ENTRADA_B(in_3), .ENTRADA_C(in_4), .ENTRADA_D(in_5), .out_7(multi_4x1_8bits_1_out_7),
    .in_4(CHAVE[1:0]), .LOAD(LOAD));
  Multi_4x1_8bits multi_4x1_8bits_2 (
    .ENTRADA_A(in_6), .ENTRADA_B(in_7), .ENTRADA_C(in_8), .ENTRADA_D(in_9), .out_7(multi_4x1_8bits_2_out_7),
    .in_4(CHAVE[1:0]), .LOAD(LOAD));
  Mult_2x1_8_bits mult_2x1_8_bits_1 (
    .A(multi_4x1_8bits_1_out_7), .B(multi_4x1_8bits_2_out_7), .\SAÍDA (\SAÍDA ), .LOAD(LOAD), .CHAVE(CHAVE[2]));
endmodule

module demultiplexador (
  input  LOAD,
  input  CLOCK,
  input  [2:0] CHAVE,
  output out_4,
  output out_5,
  output out_6,
  output out_7,
  output out_8,
  output out_9,
  output out_10,
  output out_11
);

  wire and_1_out, not_1_out, not_2_out, not_3_out, not_4_out, not_5_out, not_6_out, not_7_out, not_8_out,
       not_9_out, not_10_out, not_11_out, not_12_out;

  and and_1 (and_1_out, LOAD, CLOCK);
  not not_1 (not_1_out, CHAVE[2]);
  not not_2 (not_2_out, CHAVE[1]);
  not not_3 (not_3_out, CHAVE[0]);
  not not_4 (not_4_out, CHAVE[2]);
  not not_5 (not_5_out, CHAVE[1]);
  not not_6 (not_6_out, CHAVE[2]);
  not not_7 (not_7_out, CHAVE[0]);
  not not_8 (not_8_out, CHAVE[2]);
  not not_9 (not_9_out, CHAVE[1]);
  not not_10 (not_10_out, CHAVE[0]);
  not not_11 (not_11_out, CHAVE[1]);
  not not_12 (not_12_out, CHAVE[0]);
  and _0 (out_4, and_1_out, not_1_out, not_2_out, not_3_out);
  and _1 (out_5, and_1_out, not_4_out, not_5_out, CHAVE[0]);
  and _2 (out_6, and_1_out, not_6_out, CHAVE[1], not_7_out);
  and _3 (out_7, and_1_out, not_8_out, CHAVE[1], CHAVE[0]);
  and _4 (out_8, and_1_out, CHAVE[2], not_9_out, not_10_out);
  and _5 (out_9, and_1_out, CHAVE[2], not_11_out, CHAVE[0]);
  and _6 (out_10, and_1_out, CHAVE[2], CHAVE[1], not_12_out);
  and _7 (out_11, and_1_out, CHAVE[2], CHAVE[1], CHAVE[0]);
endmodule

module FLIP_FLOP (
  input  SET,
  input  T,
  input  CLOCK,
  input  RESET,
  output Q,
  output nQ
);

  wire nand_1_out, nand_2_out, nand_3_out, nand_4_out, nand_5_out, nand_6_out, not_1_out, not_2_out,
       not_3_out, not_4_out, not_5_out;

  not not_1 (not_1_out, CLOCK);
  not not_2 (not_2_out, T);
  nand nand_1 (nand_1_out, nQ, T, not_1_out);
  nand nand_2 (nand_2_out, not_1_out, not_2_out, Q);
  not not_3 (not_3_out, SET);
  not not_4 (not_4_out, RESET);
  nand nand_3 (nand_3_out, not_3_out, nand_1_out, nand_4_out);
  not not_5 (not_5_out, not_1_out);
  nand nand_4 (nand_4_out, nand_3_out, nand_2_out, not_4_out);
  nand nand_5 (nand_5_out, nand_3_out, not_4_out, not_5_out);
  nand nand_6 (nand_6_out, not_5_out, not_3_out, nand_4_out);
  nand nand_7 (Q, not_3_out, nand_5_out, nQ);
  nand nand_8 (nQ, Q, nand_6_out, not_4_out);
endmodule

module Registrador_8_bits (
  input  SET,
  input  CLOCK,
  input  RESET,
  input  [7:0] ENTRADA,
  output [7:0] out_5
);

  FLIP_FLOP flip_flop_1 (.SET(SET), .T(ENTRADA[0]), .Q(out_5[0]), .CLOCK(CLOCK), .RESET(RESET));  // open: nQ
  FLIP_FLOP flip_flop_2 (.SET(SET), .T(ENTRADA[1]), .Q(out_5[1]), .CLOCK(CLOCK), .RESET(RESET));  // open: nQ
  FLIP_FLOP flip_flop_3 (.SET(SET), .T(ENTRADA[2]), .Q(out_5[2]), .CLOCK(CLOCK), .RESET(RESET));  // open: nQ
  FLIP_FLOP flip_flop_4 (.SET(SET), .T(ENTRADA[3]), .Q(out_5[3]), .CLOCK(CLOCK), .RESET(RESET));  // open: nQ
  FLIP_FLOP flip_flop_5 (.SET(SET), .T(ENTRADA[4]), .Q(out_5[4]), .CLOCK(CLOCK), .RESET(RESET));  // open: nQ
  FLIP_FLOP flip_flop_6 (.SET(SET), .T(ENTRADA[5]), .Q(out_5[5]), .CLOCK(CLOCK), .RESET(RESET));  // open: nQ
  FLIP_FLOP flip_flop_7 (.SET(SET), .T(ENTRADA[6]), .Q(out_5[6]), .CLOCK(CLOCK), .RESET(RESET));  // open: nQ
  FLIP_FLOP flip_flop_8 (.SET(SET), .T(ENTRADA[7]), .Q(out_5[7]), .CLOCK(CLOCK), .RESET(RESET));  // open: nQ
endmodule
