// Logisim project somador de 8 bits.circ as structural Verilog
module somador1bit (
  input  a0,
  input  a1,
  input  cin,
  output s,
  output cout
);

  wire and_1_out, and_2_out, and_3_out, xor_1_out;

  xor xor_1 (xor_1_out, a0, a1);
  and and_1 (and_1_out, a0, a1);
  and and_2 (and_2_out, a0, cin);
  and and_3 (and_3_out, a1, cin);
  xor xor_2 (s, xor_1_out, cin);
  or or_1 (cout, and_1_out, and_2_out, and_3_out);
endmodule

module somador_4_bits (
  input  a3,
  input  a2,
  input  a1,
  input  a0,
  input  b3,
  input  b2,
  input  b1,
  input  cin,
  input  b0,
  output cout,
  output c3,
  output c2,
  output c1,
  output c0
);

  wire _1_cout, _2_cout, _3_cout;

  somador1bit _4 (.a0(a3), .a1(b3), .cin(_3_cout), .s(c3), .cout(cout));
  somador1bit _3 (.a0(a2), .a1(b2), .cin(_2_cout), .s(c2), .cout(_3_cout));
  somador1bit _2 (.a0(a1), .a1(b1), .cin(_1_cout), .s(c1), .cout(_2_cout));
  somador1bit _1 (.a0(a0), .a1(b0), .cin(cin), .s(c0), .cout(_1_cout));
endmodule

module somador_8_bits (
  input  a7,
  input  a6,
  input  a5,
  input  a4,
  input  a3,
  input  a2,
  input  a1,
  input  a0,
  input  b7,
  input  b6,
  input  b5,
  input  b4,
  input  b3,
  input  b2,
  input  b1,
  input  b0,
  input  cin,
  output cout,
  output c7,
  output c6,
  output c5,
  output c4,
  output c3,
  output c2,
  output c1,
  output c0
);

  wire _1_cout;

  somador_4_bits _2 (
    .b3(b7), .a3(a7), .b2(b6), .a2(a6), .b1(b5), .a1(a5), .cin(_1_cout), .b0(b4), .a0(a4), .cout(cout),
    .c3(c7), .c2(c6), .c1(c5), .c0(c4));
  somador_4_bits _1 (
    .b3(b3), .a3(a3), .b2(b2), .a2(a2), .b1(b1), .a1(a1), .cin(cin), .b0(b0), .a0(a0), .cout(_1_cout),
    .c3(c3), .c2(c2), .c1(c1), .c0(c0));
endmodule
