// Logisim project ULA.circ as structural Verilog: 17 circuits, main circuit main
module main (
  input  [7:0] A,
  input  [7:0] B,
  input  [3:0] SELETOR,
  output [7:0] \SAÍDA 
);

  wire [7:0] AND_out, NAND_out, NOR_out, not_1_out, OR_out, \shif_left_1_saída , \shift_right_1_saída ,
       \somador_8bts_1_saída , \subtrador_8bits_1_saída , XOR_out;

  assign AND_out = A & B;  // AND_Gate AND, 8 bits wide
  assign OR_out = A | B;  // OR_Gate OR, 8 bits wide
  assign not_1_out = ~A;  // NOT_Gate not_1, 8 bits wide
  assign NOR_out = ~(A | B);  // NOR_Gate NOR, 8 bits wide
  assign NAND_out = ~(A & B);  // NAND_Gate NAND, 8 bits wide
  assign XOR_out = A ^ B;  // XOR_Gate XOR, 8 bits wide
  shif_left shif_left_1 (.ENTRADA(A), .CHAVE(2'b10), .\SAÍDA (\shif_left_1_saída ));
  shift_right shift_right_1 (.ENTRADA(A), .CHAVE(2'b10), .\SAÍDA (\shift_right_1_saída ));
  somador_8bts somador_8bts_1 (.ENTRADA(A), .ENTRADA_2(B), .\SAÍDA (\somador_8bts_1_saída ));
  subtrador_8bits subtrador_8bits_1 (.ENTRADA(A), .ENTRADA_2(B), .\SAÍDA (\subtrador_8bits_1_saída ));
  Mult_16x1_8bits mult_16x1_8bits_1 (
    .A1(AND_out), .A2(OR_out), .A3(not_1_out), .A4(NOR_out), .A5(NAND_out), .A6(XOR_out),
    .A7(\shif_left_1_saída ), .A8(\shift_right_1_saída ), .A9(\somador_8bts_1_saída ),
    .A10(\subtrador_8bits_1_saída ), .chave(SELETOR), .\SAÍDA (\SAÍDA ));

  // Notes on the sheet:
  //   NOT
  //   SHIFT A ESQUERDA
  //   SHIFT A DIREITA
  //   SOMADOR
  //   SUBTRADOR
  //   0000 - AND
  //   0001 - OR
  //   0010 - NOT
  //   0011 - NOR
  //   0100 - NAND
  //   0101 - XOR
  //   0110 - SHIFT 2 BITS ESQUERDA
  //   0111 - SHIFT 2 BITS DIREITA
  //   1000 - SOMADOR
  //   1001 - SUBTRADOR
endmodule

module multi_2x1 (
  input  A,
  input  B,
  input  chave,
  output S
);

  wire and_1_out, and_2_out, not_1_out;

  and and_1 (and_1_out, A, not_1_out);
  not not_1 (not_1_out, chave);
  and and_2 (and_2_out, B, chave);
  or or_1 (S, and_1_out, and_2_out);
endmodule

module multi_2x1_8bits (
  input  [7:0] in_1,
  input  [7:0] in_2,
  input  chave,
  output [7:0] out_4
);

  multi_2x1 multi_2x1_1 (.A(in_1[0]), .B(in_2[0]), .S(out_4[0]), .chave(chave));
  multi_2x1 multi_2x1_2 (.A(in_1[1]), .B(in_2[1]), .S(out_4[1]), .chave(chave));
  multi_2x1 multi_2x1_3 (.A(in_1[2]), .B(in_2[2]), .S(out_4[2]), .chave(chave));
  multi_2x1 multi_2x1_4 (.A(in_1[3]), .B(in_2[3]), .S(out_4[3]), .chave(chave));
  multi_2x1 multi_2x1_5 (.A(in_1[4]), .B(in_2[4]), .S(out_4[4]), .chave(chave));
  multi_2x1 multi_2x1_6 (.A(in_1[5]), .B(in_2[5]), .S(out_4[5]), .chave(chave));
  multi_2x1 multi_2x1_7 (.A(in_1[6]), .B(in_2[6]), .S(out_4[6]), .chave(chave));
  multi_2x1 multi_2x1_8 (.A(in_1[7]), .B(in_2[7]), .S(out_4[7]), .chave(chave));
endmodule

module Mult_4x1 (
  input  in_1,
  input  in_2,
  input  in_3,
  input  in_4,
  input  S2,
  input  S1,
  output out_7
);

  wire and_1_out, and_2_out, and_3_out, and_4_out;

  and and_1 (and_1_out, in_1, ~S2, ~S1);  // AND_Gate
  and and_2 (and_2_out, in_2, ~S2, S1);  // AND_Gate
  and and_3 (and_3_out, in_3, S2, ~S1);  // AND_Gate
  and and_4 (and_4_out, in_4, S2, S1);
  or or_1 (out_7, and_1_out, and_2_out, and_3_out, and_4_out);
endmodule

module Multi_4x1_8bits (
  input  [7:0] A,
  input  [7:0] B,
  input  [1:0] CHAVE,
  input  [7:0] C,
  input  [7:0] D,
  output [7:0] \SAÍDA 
);

  Mult_4x1 mult_4x1_1 (
    .in_1(A[0]), .in_2(B[0]), .in_3(C[0]), .in_4(D[0]), .out_7(\SAÍDA [0]), .S2(CHAVE[1]), .S1(CHAVE[0]));
  Mult_4x1 mult_4x1_2 (
    .in_1(A[1]), .in_2(B[1]), .in_3(C[1]), .in_4(D[1]), .out_7(\SAÍDA [1]), .S2(CHAVE[1]), .S1(CHAVE[0]));
  Mult_4x1 mult_4x1_3 (
    .in_1(A[2]), .in_2(B[2]), .in_3(C[2]), .in_4(D[2]), .out_7(\SAÍDA [2]), .S2(CHAVE[1]), .S1(CHAVE[0]));
  Mult_4x1 mult_4x1_4 (
    .in_1(A[3]), .in_2(B[3]), .in_3(C[3]), .in_4(D[3]), .out_7(\SAÍDA [3]), .S2(CHAVE[1]), .S1(CHAVE[0]));
  Mult_4x1 mult_4x1_5 (
    .in_1(A[4]), .in_2(B[4]), .in_3(C[4]), .in_4(D[4]), .out_7(\SAÍDA [4]), .S2(CHAVE[1]), .S1(CHAVE[0]));
  Mult_4x1 mult_4x1_6 (
    .in_1(A[5]), .in_2(B[5]), .in_3(C[5]), .in_4(D[5]), .out_7(\SAÍDA [5]), .S2(CHAVE[1]), .S1(CHAVE[0]));
  Mult_4x1 mult_4x1_7 (
    .in_1(A[6]), .in_2(B[6]), .in_3(C[6]), .in_4(D[6]), .out_7(\SAÍDA [6]), .S2(CHAVE[1]), .S1(CHAVE[0]));
  Mult_4x1 mult_4x1_8 (
    .in_1(A[7]), .in_2(B[7]), .in_3(C[7]), .in_4(D[7]), .out_7(\SAÍDA [7]), .S2(CHAVE[1]), .S1(CHAVE[0]));
endmodule

module Mult_8x1_8bits (
  input  [7:0] A,
  input  [7:0] B,
  input  [7:0] C,
  input  [7:0] D,
  input  [7:0] E,
  input  [7:0] F,
  input  [7:0] G,
  input  [7:0] H,
  input  [2:0] CHAVE,
  output [7:0] SAIDA
);

  wire [7:0] \multi_4x1_8bits_1_saída , \multi_4x1_8bits_2_saída ;

  Multi_4x1_8bits multi_4x1_8bits_1 (
    .A(A), .B(B), .CHAVE(CHAVE[1:0]), .C(C), .D(D), .\SAÍDA (\multi_4x1_8bits_1_saída ));
  Multi_4x1_8bits multi_4x1_8bits_2 (
    .A(E), .B(F), .CHAVE(CHAVE[1:0]), .C(G), .D(H), .\SAÍDA (\multi_4x1_8bits_2_saída ));
  multi_2x1_8bits multi_2x1_8bits_1 (
    .in_1(\multi_4x1_8bits_1_saída ), .in_2(\multi_4x1_8bits_2_saída ), .out_4(SAIDA), .chave(CHAVE[2]));
endmodule

module Mult_16x1_8bits (
  input  [7:0] A1,
  input  [7:0] A2,
  input  [7:0] A3,
  input  [7:0] A4,
  input  [7:0] A5,
  input  [7:0] A6,
  input  [7:0] A7,
  input  [7:0] A8,
  input  [7:0] A9,
  input  [7:0] A10,
  input  [3:0] chave,
  output [7:0] \SAÍDA 
);

  wire [7:0] mult_8x1_8bits_1_saida, mult_8x1_8bits_2_saida;

  Mult_8x1_8bits mult_8x1_8bits_1 (
    .A(A1), .B(A2), .C(A3), .D(A4), .E(A5), .F(A6), .G(A7), .H(A8), .CHAVE(chave[2:0]),
    .SAIDA(mult_8x1_8bits_1_saida));
  Mult_8x1_8bits mult_8x1_8bits_2 (
    .A(A9), .B(A10), .C({8{1'b0}}), .D({8{1'b0}}), .E({8{1'b0}}), .F({8{1'b0}}), .G({8{1'b0}}),
    .H({8{1'b0}}), .CHAVE(chave[2:0]), .SAIDA(mult_8x1_8bits_2_saida));
  multi_2x1_8bits multi_2x1_8bits_1 (
    .in_1(mult_8x1_8bits_1_saida), .in_2(mult_8x1_8bits_2_saida), .out_4(\SAÍDA ), .chave(chave[3]));
endmodule

module shif_left (
  input  [7:0] ENTRADA,
  input  [1:0] CHAVE,
  output [7:0] \SAÍDA 
);

  wire and_1_out, and_2_out, and_3_out, and_4_out, and_5_out, and_6_out, and_7_out, and_8_out, and_9_out,
       and_10_out, and_11_out, and_12_out, and_13_out, and_14_out, and_15_out, and_17_out, and_18_out,
       and_19_out, and_20_out, and_21_out, and_22_out, and_23_out, and_24_out, and_25_out, and_26_out,
       and_28_out, not_1_out, not_2_out, or_1_out, or_2_out, or_3_out, or_4_out, or_5_out, or_6_out;

  not not_1 (not_1_out, CHAVE[1]);
  and and_1 (and_1_out, ENTRADA[0], CHAVE[1]);
  and and_2 (and_2_out, not_1_out, ENTRADA[1]);
  and and_3 (and_3_out, ENTRADA[1], CHAVE[1]);
  and and_4 (and_4_out, not_1_out, ENTRADA[2]);
  and and_5 (and_5_out, ENTRADA[2], CHAVE[1]);
  and and_6 (and_6_out, not_1_out, ENTRADA[3]);
  and and_7 (and_7_out, ENTRADA[3], CHAVE[1]);
  and and_8 (and_8_out, not_1_out, ENTRADA[4]);
  and and_9 (and_9_out, ENTRADA[4], CHAVE[1]);
  and and_10 (and_10_out, not_1_out, ENTRADA[5]);
  and and_11 (and_11_out, ENTRADA[5], CHAVE[1]);
  and and_12 (and_12_out, not_1_out, ENTRADA[6]);
  and and_13 (and_13_out, ENTRADA[6], CHAVE[1]);
  and and_14 (and_14_out, ENTRADA[7], not_1_out);
  or or_1 (or_1_out, and_5_out, and_8_out);
  or or_2 (or_2_out, and_7_out, and_10_out);
  or or_3 (or_3_out, and_9_out, and_12_out);
  or or_4 (or_4_out, and_11_out, and_14_out);
  or or_5 (or_5_out, and_1_out, and_4_out);
  or or_6 (or_6_out, and_3_out, and_6_out);
  not not_2 (not_2_out, CHAVE[0]);
  and and_15 (and_15_out, and_2_out, not_2_out);
  and and_16 (\SAÍDA [0], CHAVE[0], or_5_out);
  and and_17 (and_17_out, or_5_out, not_2_out);
  and and_18 (and_18_out, CHAVE[0], or_6_out);
  and and_19 (and_19_out, or_6_out, not_2_out);
  and and_20 (and_20_out, CHAVE[0], or_1_out);
  and and_21 (and_21_out, or_1_out, not_2_out);
  and and_22 (and_22_out, CHAVE[0], or_2_out);
  and and_23 (and_23_out, or_2_out, not_2_out);
  and and_24 (and_24_out, CHAVE[0], or_3_out);
  and and_25 (and_25_out, or_3_out, not_2_out);
  and and_26 (and_26_out, CHAVE[0], or_4_out);
  and and_27 (\SAÍDA [7], or_4_out, not_2_out);
  and and_28 (and_28_out, and_13_out, CHAVE[0]);
  or or_7 (\SAÍDA [5], and_23_out, and_26_out);
  or or_8 (\SAÍDA [6], and_25_out, and_28_out);
  or or_9 (\SAÍDA [1], and_15_out, and_18_out);
  or or_10 (\SAÍDA [2], and_17_out, and_20_out);
  or or_11 (\SAÍDA [3], and_19_out, and_22_out);
  or or_12 (\SAÍDA [4], and_21_out, and_24_out);
endmodule

module shift_right (
  input  [7:0] ENTRADA,
  input  [1:0] CHAVE,
  output [7:0] \SAÍDA 
);

  wire and_1_out, and_2_out, and_3_out, and_4_out, and_5_out, and_6_out, and_7_out, and_8_out, and_9_out,
       and_10_out, and_11_out, and_12_out, and_13_out, and_14_out, and_15_out, and_17_out, and_18_out,
       and_19_out, and_20_out, and_21_out, and_22_out, and_23_out, and_24_out, and_25_out, and_26_out,
       and_28_out, not_1_out, not_2_out, or_1_out, or_2_out, or_3_out, or_4_out, or_5_out, or_6_out;

  not not_1 (not_1_out, CHAVE[1]);
  and and_1 (and_1_out, ENTRADA[0], not_1_out);
  and and_2 (and_2_out, CHAVE[1], ENTRADA[1]);
  and and_3 (and_3_out, ENTRADA[1], not_1_out);
  and and_4 (and_4_out, CHAVE[1], ENTRADA[2]);
  and and_5 (and_5_out, ENTRADA[2], not_1_out);
  and and_6 (and_6_out, CHAVE[1], ENTRADA[3]);
  and and_7 (and_7_out, ENTRADA[3], not_1_out);
  and and_8 (and_8_out, CHAVE[1], ENTRADA[4]);
  and and_9 (and_9_out, ENTRADA[4], not_1_out);
  and and_10 (and_10_out, CHAVE[1], ENTRADA[5]);
  and and_11 (and_11_out, ENTRADA[5], not_1_out);
  and and_12 (and_12_out, CHAVE[1], ENTRADA[6]);
  and and_13 (and_13_out, ENTRADA[6], not_1_out);
  and and_14 (and_14_out, ENTRADA[7], CHAVE[1]);
  or or_1 (or_1_out, and_5_out, and_8_out);
  or or_2 (or_2_out, and_7_out, and_10_out);
  or or_3 (or_3_out, and_9_out, and_12_out);
  or or_4 (or_4_out, and_11_out, and_14_out);
  or or_5 (or_5_out, and_1_out, and_4_out);
  or or_6 (or_6_out, and_3_out, and_6_out);
  not not_2 (not_2_out, CHAVE[0]);
  and and_15 (and_15_out, and_2_out, CHAVE[0]);
  and and_16 (\SAÍDA [0], not_2_out, or_5_out);
  and and_17 (and_17_out, or_5_out, CHAVE[0]);
  and and_18 (and_18_out, not_2_out, or_6_out);
  and and_19 (and_19_out, or_6_out, CHAVE[0]);
  and and_20 (and_20_out, not_2_out, or_1_out);
  and and_21 (and_21_out, or_1_out, CHAVE[0]);
  and and_22 (and_22_out, not_2_out, or_2_out);
  and and_23 (and_23_out, or_2_out, CHAVE[0]);
  and and_24 (and_24_out, not_2_out, or_3_out);
  and and_25 (and_25_out, or_3_out, CHAVE[0]);
  and and_26 (and_26_out, not_2_out, or_4_out);
  and and_27 (\SAÍDA [7], or_4_out, CHAVE[0]);
  and and_28 (and_28_out, and_13_out, not_2_out);
  or or_7 (\SAÍDA [5], and_23_out, and_26_out);
  or or_8 (\SAÍDA [6], and_25_out, and_28_out);
  or or_9 (\SAÍDA [1], and_15_out, and_18_out);
  or or_10 (\SAÍDA [2], and_17_out, and_20_out);
  or or_11 (\SAÍDA [3], and_19_out, and_22_out);
  or or_12 (\SAÍDA [4], and_21_out, and_24_out);
endmodule

module meio_somador (
  input  A,
  input  B,
  output \SAÍDA ,
  output COMP
);

  xor xor_1 (\SAÍDA , A, B);
  and and_1 (COMP, A, B);
endmodule

module somador (
  input  ci,
  input  A,
  input  B,
  output soma,
  output comp
);

  wire meio_somador_1_comp, \meio_somador_1_saída , meio_somador_2_comp;

  meio_somador meio_somador_1 (.A(A), .B(B), .\SAÍDA (\meio_somador_1_saída ), .COMP(meio_somador_1_comp));
  meio_somador meio_somador_2 (.A(ci), .B(\meio_somador_1_saída ), .\SAÍDA (soma), .COMP(meio_somador_2_comp));
  or or_1 (comp, meio_somador_2_comp, meio_somador_1_comp);
endmodule

module somador_4bits (
  input  C0,
  input  A0,
  input  B0,
  input  A1,
  input  B1,
  input  A2,
  input  B2,
  input  A3,
  input  B3,
  output S0,
  output S1,
  output S2,
  output S3,
  output C4
);

  wire somador_1_comp, somador_2_comp, somador_3_comp;

  somador somador_1 (.ci(C0), .A(A0), .B(B0), .soma(S0), .comp(somador_1_comp));
  somador somador_2 (.ci(somador_1_comp), .A(A1), .B(B1), .soma(S1), .comp(somador_2_comp));
  somador somador_3 (.ci(somador_2_comp), .A(A2), .B(B2), .soma(S2), .comp(somador_3_comp));
  somador somador_4 (.ci(somador_3_comp), .A(A3), .B(B3), .soma(S3), .comp(C4));
endmodule

module somador_8bts (
  input  [7:0] ENTRADA,
  input  [7:0] ENTRADA_2,
  output [7:0] \SAÍDA 
);

  wire somador_4bits_1_c4;

  somador_4bits somador_4bits_1 (
    .C0(1'b0), .A0(ENTRADA[0]), .B0(ENTRADA_2[0]), .A1(ENTRADA[1]), .B1(ENTRADA_2[1]), .A2(ENTRADA[2]),
    .B2(ENTRADA_2[2]), .A3(ENTRADA[3]), .B3(ENTRADA_2[3]), .S0(\SAÍDA [0]), .S1(\SAÍDA [1]), .S2(\SAÍDA [2]),
    .S3(\SAÍDA [3]), .C4(somador_4bits_1_c4));
  somador_4bits somador_4bits_2 (
    .C0(somador_4bits_1_c4), .A0(ENTRADA[4]), .B0(ENTRADA_2[4]), .A1(ENTRADA[5]), .B1(ENTRADA_2[5]),
    .A2(ENTRADA[6]), .B2(ENTRADA_2[6]), .A3(ENTRADA[7]), .B3(ENTRADA_2[7]), .S0(\SAÍDA [4]), .S1(\SAÍDA [5]),
    .S2(\SAÍDA [6]), .S3(\SAÍDA [7]));  // open: C4
endmodule

module meio_subtrador (
  input  A,
  input  B,
  output \subtração ,
  output comp
);

  wire not_1_out;

  not not_1 (not_1_out, A);
  xor xor_1 (\subtração , A, B);
  and and_1 (comp, not_1_out, B);
endmodule

module subtrador (
  input  ci,
  input  A,
  input  B,
  output \subtração ,
  output comp
);

  wire meio_subtrador_1_comp, \meio_subtrador_1_subtração , meio_subtrador_2_comp;

  meio_subtrador meio_subtrador_1 (
    .A(A), .B(B), .\subtração (\meio_subtrador_1_subtração ), .comp(meio_subtrador_1_comp));
  meio_subtrador meio_subtrador_2 (
    .A(\meio_subtrador_1_subtração ), .B(ci), .\subtração (\subtração ), .comp(meio_subtrador_2_comp));
  or or_1 (comp, meio_subtrador_2_comp, meio_subtrador_1_comp);
endmodule

module subtrador_4_bits (
  input  C0,
  input  A0,
  input  B0,
  input  A1,
  input  B1,
  input  A2,
  input  B2,
  input  A3,
  input  B3,
  output S0,
  output S1,
  output S2,
  output S3,
  output C4
);

  wire subtrador_1_comp, subtrador_2_comp, subtrador_3_comp;

  subtrador subtrador_1 (.ci(C0), .A(A0), .B(B0), .\subtração (S0), .comp(subtrador_1_comp));
  subtrador subtrador_2 (.ci(subtrador_1_comp), .A(A1), .B(B1), .\subtração (S1), .comp(subtrador_2_comp));
  subtrador subtrador_3 (.ci(subtrador_2_comp), .A(A2), .B(B2), .\subtração (S2), .comp(subtrador_3_comp));
  subtrador subtrador_4 (.ci(subtrador_3_comp), .A(A3), .B(B3), .\subtração (S3), .comp(C4));
endmodule

module subtrador_8bits (
  input  [7:0] ENTRADA,
  input  [7:0] ENTRADA_2,
  output [7:0] \SAÍDA 
);

  wire subtrador_4_bits_1_c4, subtrador_4_bits_2_c4;

  subtrador_4_bits subtrador_4_bits_1 (
    .C0(1'b0), .A0(ENTRADA[0]), .B0(ENTRADA_2[0]), .A1(ENTRADA[1]), .B1(ENTRADA_2[1]), .A2(ENTRADA[2]),
    .B2(ENTRADA_2[2]), .A3(ENTRADA[3]), .B3(ENTRADA_2[3]), .S0(\SAÍDA [0]), .S1(\SAÍDA [1]), .S2(\SAÍDA [2]),
    .S3(\SAÍDA [3]), .C4(subtrador_4_bits_1_c4));
  subtrador_4_bits subtrador_4_bits_2 (
    .C0(subtrador_4_bits_1_c4), .A0(ENTRADA[4]), .B0(ENTRADA_2[4]), .A1(ENTRADA[5]), .B1(ENTRADA_2[5]),
    .A2(ENTRADA[6]), .B2(ENTRADA_2[6]), .A3(ENTRADA[7]), .B3(ENTRADA_2[7]), .S0(\SAÍDA [4]), .S1(\SAÍDA [5]),
    .S2(\SAÍDA [6]), .S3(\SAÍDA [7]), .C4(subtrador_4_bits_2_c4));
endmodule
