// Logisim project 12-Maquina-de-estado.circ as structural Verilog: 2 circuits, main circuit main
module main (
  input  in_1
);

  wire clock_1_out, semaforo_1_out_3;

  semaforo semaforo_1 (.out_3(semaforo_1_out_3), .ENTRADA(in_1));  // open: in_1
  Clock clock_1 (.out(clock_1_out));
  LED led_1 (.in(semaforo_1_out_3));
endmodule

module semaforo (
  input  in_1,
  input  ENTRADA,
  output out_3
);

  wire and_1_out, and_2_out, or_1_out;

  and and_1 (and_1_out, ~out_3, ENTRADA);  // AND_Gate
  and and_2 (and_2_out, out_3, ~ENTRADA);  // AND_Gate
  or or_1 (or_1_out, and_1_out, and_2_out);
  // flipflop_padrao flipflop_padrao_1: pin names not known; wires that end beside it: in_1, or_1_out, out_3

  // Notes on the sheet:
  //   Maquina de Estado 
endmodule
