// Logisim project Contador-sincrono.circ as structural Verilog: 3 circuits, main circuit Contador-3-bits
module Contador_3_bits (
  input  SET,
  input  RESET,
  output out_3,
  output out_4,
  output out_5
);

  wire and_1_out, CLOCK_out;

  Clock CLOCK (.out(CLOCK_out));
  and and_1 (and_1_out, out_4, out_5);
  flip_flop_t flip_flop_t_1 (.T(and_1_out), .CLOCK(CLOCK_out), .Q(out_3), .SET(SET), .RESET(RESET));  // open: nQ
  flip_flop_t flip_flop_t_2 (.T(out_5), .CLOCK(CLOCK_out), .Q(out_4), .SET(SET), .RESET(RESET));  // open: nQ
  flip_flop_t flip_flop_t_3 (.T(1'b1), .CLOCK(CLOCK_out), .Q(out_5), .SET(SET), .RESET(RESET));  // open: nQ
endmodule

module flip_flop_t (
  input  SET,
  input  T,
  input  CLOCK,
  input  RESET,
  output Q,
  output nQ
);

  wire nand_1_out, nand_2_out, nand_3_out, nand_4_out, nand_5_out, nand_6_out, not_1_out, not_2_out,
       not_3_out, not_4_out;

  not not_1 (not_1_out, CLOCK);
  nand nand_1 (nand_1_out, nQ, T, not_1_out);
  nand nand_2 (nand_2_out, not_1_out, T, Q);
  not not_2 (not_2_out, SET);
  not not_3 (not_3_out, RESET);
  nand nand_3 (nand_3_out, not_2_out, nand_1_out, nand_4_out);
  not not_4 (not_4_out, not_1_out);
  nand nand_4 (nand_4_out, nand_3_out, nand_2_out, not_3_out);
  nand nand_5 (nand_5_out, nand_3_out, not_3_out, not_4_out);
  nand nand_6 (nand_6_out, not_4_out, not_2_out, nand_4_out);
  nand nand_7 (Q, not_2_out, nand_5_out, nQ);
  nand nand_8 (nQ, Q, nand_6_out, not_3_out);
endmodule

module contandor_com_4_bits (
  input  SET,
  input  RESET,
  output out_3,
  output out_4,
  output out_5,
  output out_6
);

  wire and_1_out, and_2_out, CLOCK_out;

  and and_1 (and_1_out, out_4, and_2_out);
  Clock CLOCK (.out(CLOCK_out));
  flip_flop_t flip_flop_t_1 (.T(and_1_out), .CLOCK(CLOCK_out), .Q(out_3), .SET(SET), .RESET(RESET));  // open: nQ
  and and_2 (and_2_out, out_6, out_5, out_6);
  flip_flop_t flip_flop_t_2 (.T(and_2_out), .CLOCK(CLOCK_out), .Q(out_4), .SET(SET), .RESET(RESET));  // open: nQ
  flip_flop_t flip_flop_t_3 (.T(out_6), .CLOCK(CLOCK_out), .Q(out_5), .SET(SET), .RESET(RESET));  // open: nQ
  flip_flop_t flip_flop_t_4 (.T(1'b1), .CLOCK(CLOCK_out), .Q(out_6), .SET(SET), .RESET(RESET));  // open: nQ
endmodule
