// Logisim project detector de paridade ímpar.circ as structural Verilog: 1 circuit, main circuit main
module main (
  input  A,
  input  A_2,
  input  B,
  input  B_2,
  input  D,
  input  D_2,
  output out_7,
  output out_8
);

  wire and_1_out, and_2_out, and_3_out, and_4_out, not_1_out, not_2_out, not_3_out, not_4_out, or_1_out,
       xor_1_out;

  not not_1 (not_1_out, A_2);
  not not_2 (not_2_out, B_2);
  not not_3 (not_3_out, or_1_out);
  not not_4 (not_4_out, D_2);
  and and_1 (and_1_out, not_1_out, B_2);
  and and_2 (and_2_out, not_2_out, A_2);
  and and_3 (and_3_out, not_3_out, D_2);
  and and_4 (and_4_out, not_4_out, or_1_out);
  or or_1 (or_1_out, and_1_out, and_2_out);
  or or_2 (out_8, and_3_out, and_4_out);
  xor xor_1 (xor_1_out, A, B);
  xor xor_2 (out_7, xor_1_out, D);

  // Notes on the sheet:
  //   Detector de paridade ímpar
  //   Equivalência do circuito com portas XOR
endmodule
